# Fritzing sketch handkontroller (saved by Fritzing 0.9.8b)
stripboards: 1

parts:
  Part1 = Arduino Nano (Rev3.0) (ICSP)
  J1 = Screw terminal - 2 pins [package=THT]  # not connected
  J2 = Screw terminal - 2 pins [package=THT]  # not connected
  J3 = Screw terminal - 2 pins [package=THT]
  U1 = LCD-16X2 [package=lcd-16x2]
  LCM1602_IIC1 = LCM1602 IIC [part_number="LCM1602 IIC" chip_label="LCM1602 IIC" package="DIP (Dual Inline) [THT]"]
  S1 = Pushbutton [package="[THT]"]
  R1 = Resistor [tolerance=±5% resistance=10k package="0402 [SMD]"]
  R2 = Rotary Potentiometer (Small) [maximum_resistance=10kΩ package=THT]

nets:
  GND: Part1.GND, J3.pin1, LCM1602_IIC1.GND, S1.Pin_2, R2.leg1
  N1: Part1.D2, S1.Pin_4, R1.Pin_0
  5V: Part1.5V, J3.pin2, LCM1602_IIC1.VCC, R1.Pin_1, R2.leg2
  N2: Part1.A5, LCM1602_IIC1.SCL
  N3: Part1.A4, LCM1602_IIC1.SDA
  N4: Part1.A1, R2.wiper
  VSS: U1.VSS, LCM1602_IIC1.VSS
  VDD: U1.VDD, LCM1602_IIC1.VDD
  N5: U1.VO, LCM1602_IIC1.V0
  N6: U1.RS, LCM1602_IIC1.RS
  N7: U1.R_W, LCM1602_IIC1.RW
  N8: U1.E, LCM1602_IIC1.E
  N9: U1.DB0, LCM1602_IIC1.D0
  N10: U1.DB1, LCM1602_IIC1.D1
  N11: U1.DB2, LCM1602_IIC1.D2
  N12: U1.DB3, LCM1602_IIC1.D3
  N13: U1.DB4, LCM1602_IIC1.D4
  N14: U1.DB5, LCM1602_IIC1.D5
  N15: U1.DB6, LCM1602_IIC1.D6
  N16: U1.DB7, LCM1602_IIC1.D7
  N17: U1.A, LCM1602_IIC1.A
  N18: U1.K, LCM1602_IIC1.K

custom parts:
  LCM1602 IIC: I2C-Module to use a 1602 or 2004 LCD on with the wire.h libory Serial LCD Modul
